# Fritzing sketch phototransistor (saved by Fritzing 0.9.10b)
breadboards: 1

parts:
  R1 = Resistor [tolerance=±5% resistance=1k package="0603 [SMD]"]
  Q1 = LTR-301 [package=ltr-301]

nets:
  N1: R1.Pin_1, Q1.C

notes:
  A1
  GND
  VMAIN
  photo transistor
  Soil sensor
  Notecarrier-F
